// Logisim project SeqMultImpl (incomplete).circ as structural Verilog: 7 circuits, main circuit main
module main (
  input  [7:0] in_1,
  input  [7:0] in_2,
  input  in_3,
  input  in_4,
  output [15:0] out_5,
  output out_6
);

  wire makepositive8_1_isnegative, makepositive8_2_isnegative, ProdNegative;
  wire [7:0] makepositive8_1_numpos, makepositive8_2_numpos;

  MakePositive8 makepositive8_1 (.Num(in_1), .isNegative(makepositive8_1_isnegative), .NumPos(makepositive8_1_numpos));
  MakePositive8 makepositive8_2 (.Num(in_2), .isNegative(makepositive8_2_isnegative), .NumPos(makepositive8_2_numpos));
  xor xor_1 (ProdNegative, makepositive8_1_isnegative, makepositive8_2_isnegative);
  SeqMult seqmult_1 (
    .Multiplier(makepositive8_1_numpos), .Multiplicand(makepositive8_2_numpos), .Reset(in_4), .s(in_3),
    .P(out_5), .DONE(out_6));
endmodule

module ReverseBits (
  input  [7:0] RevIn,
  output [7:0] RevOut
);


  assign RevOut = {RevIn[0], RevIn[1], RevIn[2], RevIn[3], RevIn[4], RevIn[5], RevIn[6], RevIn[7]};
endmodule

module ShiftRightReg8 (
  input  Clk,
  input  ShiftEn,
  input  Load,
  input  Rst,
  input  [7:0] SLIn,
  output [7:0] SLOut
);

  wire [7:0] reversebits_1_revout, undriven;

  // Shift_Register shift_register_1: pin names not known; wires that end beside it: Rst, Load, ShiftEn, Clk, 1'b0
  ReverseBits reversebits_1 (.RevIn(SLIn), .RevOut(reversebits_1_revout));
  ReverseBits reversebits_2 (.RevIn(undriven), .RevOut(SLOut));
endmodule

module SeqMult (
  input  [7:0] Multiplier,
  input  [7:0] Multiplicand,
  input  Reset,
  input  s,
  output [15:0] P,
  output DONE
);

  wire clock_1_out, clock_2_out, clock_3_out, EA, EB, EP, LAInt, LBInt, nor_1_out, not_1_out, or_1_out,
       or_2_out, Psel, shift_register_1_p10, undriven_2;
  wire [7:0] shiftrightreg8_1_slout;
  wire [15:0] adder_1_out, multiplexer_1_out, undriven;

  Clock clock_1 (.out(clock_1_out));
  or or_1 (or_1_out, shift_register_1_p10, LAInt);
  // Shift_Register #(.length(16)) shift_register_1: pin names not known; wires that end beside it: Reset, or_1_out, EA, clock_1_out, 1'b0, 1'b0, 1'b0, 1'b0, 1'b0, shift_register_1_p10
  or or_2 (or_2_out, undriven_2, LBInt);
  Clock clock_2 (.out(clock_2_out));
  Adder #(.width(16)) adder_1 (.a(P), .b(undriven), .out(adder_1_out));  // open: cin, cout
  not not_1 (not_1_out, Psel);
  Multiplexer #(.width(16)) multiplexer_1 (
    .in0({16{1'b0}}), .in1(adder_1_out), .out(multiplexer_1_out), .sel(not_1_out));
  Register #(.width(16)) PReg (.D(multiplexer_1_out), .en(EP), .clk(clock_3_out), .Q(P), .clr(Reset));
  Clock clock_3 (.out(clock_3_out));
  ShiftRightReg8 shiftrightreg8_1 (
    .Clk(clock_2_out), .ShiftEn(EB), .Load(or_2_out), .Rst(Reset), .SLIn(Multiplier),
    .SLOut(shiftrightreg8_1_slout));
  nor nor_1 (nor_1_out, shiftrightreg8_1_slout[7], shiftrightreg8_1_slout[6], shiftrightreg8_1_slout[5], shiftrightreg8_1_slout[4], shiftrightreg8_1_slout[3], shiftrightreg8_1_slout[2], shiftrightreg8_1_slout[1], shiftrightreg8_1_slout[0]);
  ControlUnit controlunit_1 (
    .rst(Reset), .b0(shiftrightreg8_1_slout[0]), .z(nor_1_out), .s(s), .Psel(Psel), .LA(LAInt), .LB(LBInt),
    .EA(EA), .DONE(DONE), .EB(EB), .EP(EP));

  // Other names for the same wires on the sheet: Rst = Reset

  // Notes on the sheet:
  //   A
  //   B
  //   b0
  //   z
endmodule

module ControlUnit (
  input  rst,
  input  b0,
  input  z,
  input  s,
  output Psel,
  output LA,
  output LB,
  output EA,
  output DONE,
  output EB,
  output EP
);

  wire and_1_out, and_3_out, and_4_out, and_6_out, and_7_out, and_8_out, clock_1_out, clock_2_out,
       clock_3_out, not_1_out, not_2_out, not_3_out, not_4_out, or_1_out, or_2_out, or_3_out;

  or or_1 (or_1_out, and_8_out, and_1_out);
  D_Flip_Flop S1 (.D(or_1_out), .clk(clock_1_out), .Q(Psel), .preset(rst));  // open: Qn, reset
  Clock clock_1 (.out(clock_1_out));
  not not_1 (not_1_out, s);
  and and_1 (and_1_out, Psel, not_1_out);
  and and_2 (LA, s, Psel);
  or or_2 (or_2_out, LA, and_3_out, EP);
  Clock clock_2 (.out(clock_2_out));
  not not_2 (not_2_out, b0);
  and and_3 (and_3_out, and_4_out, not_2_out);
  D_Flip_Flop S2 (.D(or_2_out), .clk(clock_2_out), .Q(EA), .reset(rst));  // open: Qn, preset
  not not_3 (not_3_out, z);
  and and_4 (and_4_out, EA, not_3_out);
  and and_5 (EP, b0, and_4_out);
  and and_6 (and_6_out, z, EA);
  or or_3 (or_3_out, and_6_out, and_7_out);
  D_Flip_Flop S3 (.D(or_3_out), .clk(clock_3_out), .Q(DONE), .reset(rst));  // open: Qn, preset
  Clock clock_3 (.out(clock_3_out));
  and and_7 (and_7_out, DONE, s);
  not not_4 (not_4_out, s);
  and and_8 (and_8_out, not_4_out, DONE);

  assign EB = EA;
  assign LB = LA;
endmodule

module MakePositive8 (
  input  [7:0] Num,
  output isNegative,
  output [7:0] NumPos
);

  wire [7:0] negator_1_out;

  Negator negator_1 (.in(Num), .out(negator_1_out));
  Multiplexer #(.width(8)) multiplexer_1 (.in0(Num), .in1(negator_1_out), .out(NumPos), .sel(Num[7]));

  assign isNegative = Num[7];
endmodule

module Modulo8 (
  input  [7:0] a,
  input  rst
);

  wire clock_1_out, d_ff_1_q, ER;
  wire [7:0] multiplexer_1_out, Q, ResIn;

  Multiplexer #(.width(8)) multiplexer_1 (.in0(a), .in1(ResIn), .out(multiplexer_1_out));  // open: sel
  Register register_1 (.D(multiplexer_1_out), .en(ER), .clk(clock_1_out), .Q(Q), .clr(rst));
  Clock clock_1 (.out(clock_1_out));
  D_Flip_Flop d_ff_1 (.Q(d_ff_1_q));  // open: D, clk, Qn, preset, reset
endmodule
